# Fritzing sketch piezas_01_02 (saved by Fritzing 1.0.1rc)
breadboards: 2

parts:
  ESP32_WROOM = LuaNode32 / ESP32 [part_number="ESP32 WROOM (PIN30)"]
  SR_602_PIR_MODULE = PIR sensor  # not connected
  LCD_DISPLAY_WITH_I2C_MODULE = Standard LCD 16x2 white on blue [part_number=181]
  WAGO_221-413_splicing_connectors = Camdenboss CTB0158-3 [part_number=CTB0158-3 package=THT]
  J2 = Camdenboss CTB0158-3 [part_number=CTB0158-3 package=THT]
  SPEAKER = SPEAKER [package=pcb_mount_speaker]
  USB_CABLE = USB TTL Serial Cable
  LM386_AMPLIFIER_MODULE = LM386 [package=dip08]

nets:
  N1: ESP32_WROOM.D25, LM386_AMPLIFIER_MODULE.+IN
  N2: ESP32_WROOM.GND, J2.terminal_3
  N3: ESP32_WROOM.3V3, LM386_AMPLIFIER_MODULE.V+
  N4: ESP32_WROOM.D21, LCD_DISPLAY_WITH_I2C_MODULE.V0
  N5: ESP32_WROOM.D22, LCD_DISPLAY_WITH_I2C_MODULE.RS
  N6: LCD_DISPLAY_WITH_I2C_MODULE.VSS, J2.terminal_1
  N7: LCD_DISPLAY_WITH_I2C_MODULE.VDD, WAGO_221-413_splicing_connectors.terminal_2
  N8: WAGO_221-413_splicing_connectors.terminal_1, USB_CABLE.5V
  N9: J2.terminal_2, USB_CABLE.GND
  N10: SPEAKER.+, LM386_AMPLIFIER_MODULE.V-
  N11: SPEAKER.-, LM386_AMPLIFIER_MODULE.OUT

notes:
  Wiring diagram for boards nr. 1 and 2 (they share one microcontroller)
  __________________________________
  from the electronic and digital ensamblage Conversatorio 2023 by Silvia Binda Heiserova

custom parts:
  LuaNode32 / ESP32: New Image for LuaNode32 DOIT ESP32 DEVKIT V1. Base parts from LuaNode32 / ESP32 ESP32 based LuaNode32 by G.Noorlander DOIT Esp32 DevKit v1 (30 pins long, 11 pins width) by Werner Rothschopf (modified by vanepp Dec 2018)
  Standard LCD 16x2 white on blue: Standard HD44780 LCDs are useful for creating standalone projects. * 16 characters wide, 2 rows * White text on blue background * Connection port is 0.1" pitch, single row for easy breadboarding and wiring
