# Fritzing sketch pieza_03 (saved by Fritzing 1.0.1rc)
breadboards: 1

parts:
  SPEAKER = SPEAKER [package=pcb_mount_speaker]
  LM386_AMPLIFIER_MODULE = LM386 [package=dip08]
  Arduino_UNO = Arduino Uno (Rev3) - ICSP
  LED2 = LED - 3mm [color="Red (633nm)" current=0.030A package="3 mm [THT]"]
  LED3 = LED - 3mm [color="Red (633nm)" current=0.030A package="3 mm [THT]"]
  LED4 = LED - 3mm [color="Red (633nm)" current=0.030A package="3 mm [THT]"]
  R1 = Resistor [tolerance=±5% resistance=220 package="1206 [SMD]"]
  R2 = Resistor [tolerance=±5% resistance=220 package="1206 [SMD]"]
  R3 = Resistor [tolerance=±5% resistance=220 package="1206 [SMD]"]
  LV-MaxSonar-EZ0_ultrasonic_range_finder = Maxbotix MaxSonar Ultrasonic Sensor

nets:
  N1: SPEAKER.+, LM386_AMPLIFIER_MODULE.V-
  N2: SPEAKER.-, LM386_AMPLIFIER_MODULE.OUT
  GND: LM386_AMPLIFIER_MODULE.-IN, Arduino_UNO.GND, R1.Pin_1, R2.Pin_1, R3.Pin_1, LV-MaxSonar-EZ0_ultrasonic_range_finder.GND
  N3: LM386_AMPLIFIER_MODULE.+IN, Arduino_UNO.D6_PWM
  N4: LM386_AMPLIFIER_MODULE.V+, Arduino_UNO.3V3
  N5: Arduino_UNO.D9_PWM, LED4.cathode
  N6: Arduino_UNO.D10_PWM/SS, LED2.cathode
  N7: Arduino_UNO.D11_PWM/MOSI, LED3.cathode
  N8: Arduino_UNO.D3_PWM, LV-MaxSonar-EZ0_ultrasonic_range_finder.TX
  N9: Arduino_UNO.D4, LV-MaxSonar-EZ0_ultrasonic_range_finder.RX
  VIN: Arduino_UNO.VIN, LV-MaxSonar-EZ0_ultrasonic_range_finder.+5V
  N10: LED2.anode, R2.Pin_0
  N11: LED3.anode, R1.Pin_0
  N12: LED4.anode, R3.Pin_0

notes:
  Wiring diagram for board nr.3 __________________________________
  from the electronic and digital ensamblage Conversatorio 2023 by Silvia Binda Heiserova

custom parts:
  Maxbotix MaxSonar Ultrasonic Sensor: Maxbotix MaxSonar Ultrasonic Sensor LV-EZ0, LV-EZ1, LV-EZ2, LV-EZ3, LV-EZ4
