# Fritzing sketch pieza_4_oled_eng (saved by Fritzing 1.0.1rc)

parts:
  part = LuaNode32 / ESP32 [part_number="ESP32 WROOM (PIN30)"]
  RGB_LED = KY-016 RGB Full Color LED Module [package="Breakout board"]
  0_91''OLED_display_(blue) = OLED 0.91" 128x32 I2C SSD1306 (GND/VCC)

nets:
  N1: part.D26, RGB_LED.B
  N2: part.D27, RGB_LED.G
  N3: part.D13, RGB_LED.R
  GND: part.GND, RGB_LED.-, 0_91''OLED_display_(blue).GND
  3V3: part.3V3, 0_91''OLED_display_(blue).VCC
  N4: part.D21, 0_91''OLED_display_(blue).SCA
  N5: part.D22, 0_91''OLED_display_(blue).SCL

notes:
  Wiring diagram for board nr. 4
  __________________________________
  from the electronic and digital ensamblage Conversatorio 2023 by Silvia Binda Heiserova

custom parts:
  LuaNode32 / ESP32: New Image for LuaNode32 DOIT ESP32 DEVKIT V1. Base parts from LuaNode32 / ESP32 ESP32 based LuaNode32 by G.Noorlander DOIT Esp32 DevKit v1 (30 pins long, 11 pins width) by Werner Rothschopf (modified by vanepp Dec 2018)
  KY-016 RGB Full Color LED Module: KY-016 Arduino full color 5mm RGB LED, different colors can be obtained by mixing the three primary colors.
  OLED 0.91" 128x32 I2C SSD1306 (GND/VCC): OLED 0.91" 128x32 I2C SSD1306 Pinout: GND/VCC/SCL/SDA
