# Fritzing sketch pieza_05_laser (saved by Fritzing 1.0.1rc)

parts:
  ESP32_WROOM = LuaNode32 / ESP32 [part_number="ESP32 WROOM (PIN30)"]
  RGB_LED_(common_anode) = RGB LED (com. anode, rbg) [color="Red (633nm)" current=0.030A package="5 mm [THT]"]
  KY-008_LASER_MODULE = KY-008 Laser Transmitter Module [package="Breakout board"]

nets:
  N1: ESP32_WROOM.Vin, RGB_LED_(common_anode).common_anode
  N2: ESP32_WROOM.3V3, KY-008_LASER_MODULE.-
  N3: ESP32_WROOM.GND, KY-008_LASER_MODULE.NC
  N4: ESP32_WROOM.D15, KY-008_LASER_MODULE.S
  N5: ESP32_WROOM.D21, RGB_LED_(common_anode).red_cathode
  N6: ESP32_WROOM.D22, RGB_LED_(common_anode).blue_cathode
  N7: ESP32_WROOM.D23, RGB_LED_(common_anode).green_cathode

notes:
  Wiring diagram for board nr.5
  __________________________________
  from the electronic and digital ensamblage Conversatorio 2023 by Silvia Binda Heiserova

custom parts:
  LuaNode32 / ESP32: New Image for LuaNode32 DOIT ESP32 DEVKIT V1. Base parts from LuaNode32 / ESP32 ESP32 based LuaNode32 by G.Noorlander DOIT Esp32 DevKit v1 (30 pins long, 11 pins width) by Werner Rothschopf (modified by vanepp Dec 2018)
  KY-008 Laser Transmitter Module: KY-008 Laser Transmitter Module, emits a dot shaped red laser beam.
