# Fritzing sketch pieza_06 (saved by Fritzing 1.0.1rc)
breadboards: 8

parts:
  LED2 = LED - 3mm [color="Blue (470nm)" current=0.030A package="3 mm [THT]"]
  LED3 = LED - 3mm [color="Blue (470nm)" current=0.030A package="3 mm [THT]"]
  LED4 = LED - 3mm [color="Blue (470nm)" current=0.030A package="3 mm [THT]"]
  R1 = Resistor [tolerance=±5% resistance=220 package="1206 [SMD]"]
  R2 = Resistor [tolerance=±5% resistance=220 package="1206 [SMD]"]
  R3 = Resistor [tolerance=±5% resistance=220 package="1206 [SMD]"]
  ESP32_WROOM = LuaNode32 / ESP32 [part_number=ESP32S-PIN30]
  LED5 = LED - 3mm [color="Blue (470nm)" current=0.030A package="3 mm [THT]"]
  LED6 = LED - 3mm [color="Blue (470nm)" current=0.030A package="3 mm [THT]"]
  LED7 = LED - 3mm [color="Blue (470nm)" current=0.030A package="3 mm [THT]"]
  R4 = Resistor [tolerance=±5% resistance=220 package="1206 [SMD]"]
  R5 = Resistor [tolerance=±5% resistance=220 package="1206 [SMD]"]
  R6 = Resistor [tolerance=±5% resistance=220 package="1206 [SMD]"]
  LED8 = LED - 3mm [color="Blue (470nm)" current=0.030A package="3 mm [THT]"]
  LED9 = LED - 3mm [color="Blue (470nm)" current=0.030A package="3 mm [THT]"]
  LED10 = LED - 3mm [color="Blue (470nm)" current=0.030A package="3 mm [THT]"]
  R7 = Resistor [tolerance=±5% resistance=220 package="1206 [SMD]"]
  R8 = Resistor [tolerance=±5% resistance=220 package="1206 [SMD]"]
  R9 = Resistor [tolerance=±5% resistance=220 package="1206 [SMD]"]
  LED11 = LED - 3mm [color="Blue (470nm)" current=0.030A package="3 mm [THT]"]
  LED12 = LED - 3mm [color="Blue (470nm)" current=0.030A package="3 mm [THT]"]
  LED13 = LED - 3mm [color="Blue (470nm)" current=0.030A package="3 mm [THT]"]
  R10 = Resistor [tolerance=±5% resistance=220 package="1206 [SMD]"]
  R11 = Resistor [tolerance=±5% resistance=220 package="1206 [SMD]"]
  R12 = Resistor [tolerance=±5% resistance=220 package="1206 [SMD]"]
  LED14 = LED - 3mm [color="Blue (470nm)" current=0.030A package="3 mm [THT]"]
  LED15 = LED - 3mm [color="Blue (470nm)" current=0.030A package="3 mm [THT]"]
  LED16 = LED - 3mm [color="Blue (470nm)" current=0.030A package="3 mm [THT]"]
  R13 = Resistor [tolerance=±5% resistance=220 package="1206 [SMD]"]
  R14 = Resistor [tolerance=±5% resistance=220 package="1206 [SMD]"]
  R15 = Resistor [tolerance=±5% resistance=220 package="1206 [SMD]"]
  LED17 = LED - 3mm [color="Blue (470nm)" current=0.030A package="3 mm [THT]"]
  LED18 = LED - 3mm [color="Blue (470nm)" current=0.030A package="3 mm [THT]"]
  LED19 = LED - 3mm [color="Blue (470nm)" current=0.030A package="3 mm [THT]"]
  R16 = Resistor [tolerance=±5% resistance=220 package="1206 [SMD]"]
  R17 = Resistor [tolerance=±5% resistance=220 package="1206 [SMD]"]
  R18 = Resistor [tolerance=±5% resistance=220 package="1206 [SMD]"]
  LED20 = LED - 3mm [color="Blue (470nm)" current=0.030A package="3 mm [THT]"]
  LED23 = LED - 3mm [color="Blue (470nm)" current=0.030A package="3 mm [THT]"]
  LED26 = LED - 3mm [color="Blue (470nm)" current=0.030A package="3 mm [THT]"]
  R19 = Resistor [tolerance=±5% resistance=220 package="1206 [SMD]"]
  R20 = Resistor [tolerance=±5% resistance=220 package="1206 [SMD]"]
  R21 = Resistor [tolerance=±5% resistance=220 package="1206 [SMD]"]

nets:
  N1: LED2.cathode, LED3.cathode, LED4.cathode, ESP32_WROOM.D23
  N2: LED2.anode, R2.Pin_0
  N3: LED3.anode, R1.Pin_0
  N4: LED4.anode, R3.Pin_0
  N5: R1.Pin_1, R2.Pin_1, R3.Pin_1, ESP32_WROOM.GND, R4.Pin_1, R5.Pin_1, R6.Pin_1, R7.Pin_1, R8.Pin_1, R9.Pin_1, R10.Pin_1, R11.Pin_1, R12.Pin_1, R13.Pin_1, R14.Pin_1, R15.Pin_1, R16.Pin_1, R17.Pin_1, R18.Pin_1, R19.Pin_1, R20.Pin_1, R21.Pin_1
  N6: ESP32_WROOM.D25, LED20.cathode, LED23.cathode, LED26.cathode
  N7: ESP32_WROOM.D26, LED17.cathode, LED18.cathode, LED19.cathode
  N8: ESP32_WROOM.D27, LED5.cathode, LED6.cathode, LED7.cathode
  N9: ESP32_WROOM.D18, LED11.cathode, LED12.cathode, LED13.cathode
  N10: ESP32_WROOM.D19, LED14.cathode, LED15.cathode, LED16.cathode
  N11: ESP32_WROOM.D22, LED8.cathode, LED9.cathode, LED10.cathode
  N12: LED5.anode, R6.Pin_0
  N13: LED6.anode, R4.Pin_0
  N14: LED7.anode, R5.Pin_0
  N15: LED8.anode, R9.Pin_0
  N16: LED9.anode, R7.Pin_0
  N17: LED10.anode, R8.Pin_0
  N18: LED11.anode, R12.Pin_0
  N19: LED12.anode, R10.Pin_0
  N20: LED13.anode, R11.Pin_0
  N21: LED14.anode, R15.Pin_0
  N22: LED15.anode, R13.Pin_0
  N23: LED16.anode, R14.Pin_0
  N24: LED17.anode, R18.Pin_0
  N25: LED18.anode, R16.Pin_0
  N26: LED19.anode, R17.Pin_0
  N27: LED20.anode, R21.Pin_0
  N28: LED23.anode, R19.Pin_0
  N29: LED26.anode, R20.Pin_0

notes:
  Wiring diagram for board nr.6 __________________________________
  from the electronic and digital ensamblage Conversatorio 2023 by Silvia Binda Heiserova

custom parts:
  LuaNode32 / ESP32: New Image for LuaNode32 DOIT ESP32 DEVKIT V1. Base parts from LuaNode32 / ESP32 ESP32 based LuaNode32 by G.Noorlander DOIT Esp32 DevKit v1 (30 pins long, 11 pins width) by Werner Rothschopf (modified by vanepp Dec 2018)
