# Fritzing sketch pieza_7_osc (saved by Fritzing 1.0.1rc)

parts:
  0_91''OLED_display_(blue) = OLED 0.91" 128x32 I2C SSD1306 (GND/VCC)
  SPEAKER = SPEAKER [package=pcb_mount_speaker]
  LM386_AMPLIFIER_MODULE1 = LM386 [package=dip08]
  ESP32_WROOM1 = LuaNode32 / ESP32 [part_number="ESP32 WROOM (PIN30)"]

nets:
  GND: 0_91''OLED_display_(blue).GND, LM386_AMPLIFIER_MODULE1.-IN, ESP32_WROOM1.GND
  VCC: 0_91''OLED_display_(blue).VCC, ESP32_WROOM1.3V3
  N1: 0_91''OLED_display_(blue).SCL, ESP32_WROOM1.D22
  N2: 0_91''OLED_display_(blue).SCA, ESP32_WROOM1.D21
  N3: SPEAKER.+, LM386_AMPLIFIER_MODULE1.V-
  N4: SPEAKER.-, LM386_AMPLIFIER_MODULE1.OUT
  N5: LM386_AMPLIFIER_MODULE1.+IN, ESP32_WROOM1.D25
  N6: LM386_AMPLIFIER_MODULE1.V+, ESP32_WROOM1.Vin

notes:
  Wiring diagram for board nr. 7
  __________________________________
  from the electronic and digital ensamblage Conversatorio 2023 by Silvia Binda Heiserova

custom parts:
  OLED 0.91" 128x32 I2C SSD1306 (GND/VCC): OLED 0.91" 128x32 I2C SSD1306 Pinout: GND/VCC/SCL/SDA
  LuaNode32 / ESP32: New Image for LuaNode32 DOIT ESP32 DEVKIT V1. Base parts from LuaNode32 / ESP32 ESP32 based LuaNode32 by G.Noorlander DOIT Esp32 DevKit v1 (30 pins long, 11 pins width) by Werner Rothschopf (modified by vanepp Dec 2018)
